// Logisim project minutes_seconds2.circ as structural Verilog: 1 circuit, main circuit main
module main (
  input  in_1,
  input  in_2,
  input  in_3,
  input  in_4,
  input  in_5,
  input  in_6,
  input  in_7,
  input  in_8,
  input  in_9,
  input  in_10,
  input  in_11,
  input  in_12,
  input  in_13,
  input  in_14,
  input  in_15,
  input  in_16,
  input  in_17,
  input  in_18,
  input  in_19,
  input  in_20,
  input  in_21,
  input  in_22,
  input  in_23,
  input  in_24,
  input  in_25,
  input  in_26,
  input  in_27,
  input  in_28,
  input  in_29,
  input  in_30
);

  wire and_1_out, and_2_out, and_3_out, and_4_out, and_5_out, and_6_out, bcd_to_7_segment_decoder_1_p1,
       bcd_to_7_segment_decoder_1_p2, bcd_to_7_segment_decoder_1_p3, bcd_to_7_segment_decoder_1_p4,
       bcd_to_7_segment_decoder_1_p6, bcd_to_7_segment_decoder_1_p7, bcd_to_7_segment_decoder_1_p8,
       bcd_to_7_segment_decoder_2_p1, bcd_to_7_segment_decoder_2_p2, bcd_to_7_segment_decoder_2_p3,
       bcd_to_7_segment_decoder_2_p4, bcd_to_7_segment_decoder_2_p6, bcd_to_7_segment_decoder_2_p7,
       bcd_to_7_segment_decoder_2_p8, bcd_to_7_segment_decoder_3_p1, bcd_to_7_segment_decoder_3_p2,
       bcd_to_7_segment_decoder_3_p3, bcd_to_7_segment_decoder_3_p4, bcd_to_7_segment_decoder_3_p6,
       bcd_to_7_segment_decoder_3_p7, bcd_to_7_segment_decoder_3_p8, bcd_to_7_segment_decoder_4_p1,
       bcd_to_7_segment_decoder_4_p2, bcd_to_7_segment_decoder_4_p3, bcd_to_7_segment_decoder_4_p4,
       bcd_to_7_segment_decoder_4_p6, bcd_to_7_segment_decoder_4_p7, bcd_to_7_segment_decoder_4_p8,
       bcd_to_7_segment_decoder_5_p1, bcd_to_7_segment_decoder_5_p2, bcd_to_7_segment_decoder_5_p3,
       bcd_to_7_segment_decoder_5_p4, bcd_to_7_segment_decoder_5_p6, bcd_to_7_segment_decoder_5_p7,
       bcd_to_7_segment_decoder_5_p8, bcd_to_7_segment_decoder_6_p1, bcd_to_7_segment_decoder_6_p2,
       bcd_to_7_segment_decoder_6_p3, bcd_to_7_segment_decoder_6_p4, bcd_to_7_segment_decoder_6_p6,
       bcd_to_7_segment_decoder_6_p7, bcd_to_7_segment_decoder_6_p8, clock_1_out;
  wire [2:0] counter_3_q, counter_5_q, counter_6_q;
  wire [3:0] counter_1_q, counter_2_q, counter_4_q;

  Clock clock_1 (.out(clock_1_out));
  Counter #(.max('hf), .width(4)) counter_1 (
    .clr(in_1), .load(and_1_out), .count(1'b1), .clk(clock_1_out), .D({in_5, in_4, in_3, in_2}),
    .Q(counter_1_q));  // open: up, carry
  Counter #(.max('hf), .width(4)) counter_2 (
    .clr(in_21), .load(and_3_out), .count(and_5_out), .clk(clock_1_out), .D({in_25, in_24, in_23, in_22}),
    .Q(counter_2_q));  // open: up, carry
  Counter #(.max('h7), .width(3)) counter_3 (
    .clr(in_6), .load(and_2_out), .count(and_1_out), .clk(clock_1_out), .D({in_9, in_8, in_7}),
    .Q(counter_3_q));  // open: up, carry
  Counter #(.max('hf), .width(4)) counter_4 (
    .clr(in_11), .load(and_6_out), .count(and_2_out), .clk(clock_1_out), .D({in_15, in_14, in_13, in_12}),
    .Q(counter_4_q));  // open: up, carry
  Counter #(.max('h7), .width(3)) counter_5 (
    .clr(in_16), .load(and_5_out), .count(and_6_out), .clk(clock_1_out), .D({in_19, in_18, in_17}),
    .Q(counter_5_q));  // open: up, carry
  Counter #(.max('h7), .width(3)) counter_6 (
    .clr(in_26), .load(and_4_out), .count(and_3_out), .clk(clock_1_out), .D({in_29, in_28, in_27}),
    .Q(counter_6_q));  // open: up, carry
  and and_1 (and_1_out, counter_1_q[0], counter_1_q[3]);
  and and_2 (and_2_out, counter_3_q[0], and_1_out, counter_3_q[2]);
  and and_3 (and_3_out, counter_2_q[0], and_5_out, counter_2_q[3]);
  and and_4 (and_4_out, counter_6_q[0], and_3_out, counter_6_q[2]);
  and and_5 (and_5_out, counter_5_q[2], and_6_out, counter_5_q[0]);
  and and_6 (and_6_out, counter_4_q[3], and_2_out, counter_4_q[0]);
  // BCD_to_7_Segment_decoder bcd_to_7_segment_decoder_1: pin names not known; wires that end beside it: bcd_to_7_segment_decoder_1_p1, bcd_to_7_segment_decoder_1_p2, bcd_to_7_segment_decoder_1_p3, bcd_to_7_segment_decoder_1_p4, {in_10, counter_3_q}, bcd_to_7_segment_decoder_1_p6, bcd_to_7_segment_decoder_1_p7, bcd_to_7_segment_decoder_1_p8
  // BCD_to_7_Segment_decoder bcd_to_7_segment_decoder_2: pin names not known; wires that end beside it: bcd_to_7_segment_decoder_2_p1, bcd_to_7_segment_decoder_2_p2, bcd_to_7_segment_decoder_2_p3, bcd_to_7_segment_decoder_2_p4, {in_30, counter_6_q}, bcd_to_7_segment_decoder_2_p6, bcd_to_7_segment_decoder_2_p7, bcd_to_7_segment_decoder_2_p8
  // BCD_to_7_Segment_decoder bcd_to_7_segment_decoder_3: pin names not known; wires that end beside it: bcd_to_7_segment_decoder_3_p1, bcd_to_7_segment_decoder_3_p2, bcd_to_7_segment_decoder_3_p3, bcd_to_7_segment_decoder_3_p4, {in_20, counter_5_q}, bcd_to_7_segment_decoder_3_p6, bcd_to_7_segment_decoder_3_p7, bcd_to_7_segment_decoder_3_p8
  // BCD_to_7_Segment_decoder bcd_to_7_segment_decoder_4: pin names not known; wires that end beside it: bcd_to_7_segment_decoder_4_p1, bcd_to_7_segment_decoder_4_p2, bcd_to_7_segment_decoder_4_p3, bcd_to_7_segment_decoder_4_p4, counter_1_q, bcd_to_7_segment_decoder_4_p6, bcd_to_7_segment_decoder_4_p7, bcd_to_7_segment_decoder_4_p8
  // BCD_to_7_Segment_decoder bcd_to_7_segment_decoder_5: pin names not known; wires that end beside it: bcd_to_7_segment_decoder_5_p1, bcd_to_7_segment_decoder_5_p2, bcd_to_7_segment_decoder_5_p3, bcd_to_7_segment_decoder_5_p4, counter_4_q, bcd_to_7_segment_decoder_5_p6, bcd_to_7_segment_decoder_5_p7, bcd_to_7_segment_decoder_5_p8
  // BCD_to_7_Segment_decoder bcd_to_7_segment_decoder_6: pin names not known; wires that end beside it: bcd_to_7_segment_decoder_6_p1, bcd_to_7_segment_decoder_6_p2, bcd_to_7_segment_decoder_6_p3, bcd_to_7_segment_decoder_6_p4, counter_2_q, bcd_to_7_segment_decoder_6_p6, bcd_to_7_segment_decoder_6_p7, bcd_to_7_segment_decoder_6_p8
  _7_Segment_Display u_7_segment_display_1 (
    .g(bcd_to_7_segment_decoder_3_p1), .f(bcd_to_7_segment_decoder_3_p3), .a(bcd_to_7_segment_decoder_3_p6),
    .b(bcd_to_7_segment_decoder_3_p8), .e(bcd_to_7_segment_decoder_3_p2), .d(bcd_to_7_segment_decoder_3_p4),
    .c(bcd_to_7_segment_decoder_3_p7));  // open: dp
  _7_Segment_Display u_7_segment_display_2 (
    .g(bcd_to_7_segment_decoder_2_p1), .f(bcd_to_7_segment_decoder_2_p3), .a(bcd_to_7_segment_decoder_2_p6),
    .b(bcd_to_7_segment_decoder_2_p8), .e(bcd_to_7_segment_decoder_2_p2), .d(bcd_to_7_segment_decoder_2_p4),
    .c(bcd_to_7_segment_decoder_2_p7));  // open: dp
  _7_Segment_Display u_7_segment_display_3 (
    .g(bcd_to_7_segment_decoder_5_p1), .f(bcd_to_7_segment_decoder_5_p3), .a(bcd_to_7_segment_decoder_5_p6),
    .b(bcd_to_7_segment_decoder_5_p8), .e(bcd_to_7_segment_decoder_5_p2), .d(bcd_to_7_segment_decoder_5_p4),
    .c(bcd_to_7_segment_decoder_5_p7));  // open: dp
  _7_Segment_Display u_7_segment_display_4 (
    .g(bcd_to_7_segment_decoder_6_p1), .f(bcd_to_7_segment_decoder_6_p3), .a(bcd_to_7_segment_decoder_6_p6),
    .b(bcd_to_7_segment_decoder_6_p8), .e(bcd_to_7_segment_decoder_6_p2), .d(bcd_to_7_segment_decoder_6_p4),
    .c(bcd_to_7_segment_decoder_6_p7));  // open: dp
  _7_Segment_Display u_7_segment_display_5 (
    .g(bcd_to_7_segment_decoder_1_p1), .f(bcd_to_7_segment_decoder_1_p3), .a(bcd_to_7_segment_decoder_1_p6),
    .b(bcd_to_7_segment_decoder_1_p8), .e(bcd_to_7_segment_decoder_1_p2), .d(bcd_to_7_segment_decoder_1_p4),
    .c(bcd_to_7_segment_decoder_1_p7));  // open: dp
  _7_Segment_Display u_7_segment_display_6 (
    .g(bcd_to_7_segment_decoder_4_p1), .f(bcd_to_7_segment_decoder_4_p3), .a(bcd_to_7_segment_decoder_4_p6),
    .b(bcd_to_7_segment_decoder_4_p8), .e(bcd_to_7_segment_decoder_4_p2), .d(bcd_to_7_segment_decoder_4_p4),
    .c(bcd_to_7_segment_decoder_4_p7));  // open: dp
endmodule
