// Logisim project minutes_seconds2_final.circ as structural Verilog: 2 circuits, main circuit main
// 3
module main (
  input  in_1,
  input  in_2,
  input  in_3,
  input  in_4,
  input  in_5,
  input  BTNC,
  input  in_7,
  input  in_8,
  input  in_9,
  input  in_10,
  input  in_11,
  input  in_12,
  input  in_13,
  input  in_14,
  input  in_15,
  input  in_16,
  input  in_17,
  input  in_18,
  input  in_19,
  input  in_20,
  input  in_21
);

  wire and_1_out, and_2_out, and_3_out, and_4_out, and_5_out, and_6_out, and_7_out, and_8_out, and_9_out,
       and_10_out, and_11_out, and_12_out, and_13_out, bcd_to_7_segment_decoder_1_p1,
       bcd_to_7_segment_decoder_1_p2, bcd_to_7_segment_decoder_1_p3, bcd_to_7_segment_decoder_1_p4,
       bcd_to_7_segment_decoder_1_p6, bcd_to_7_segment_decoder_1_p7, bcd_to_7_segment_decoder_1_p8,
       bcd_to_7_segment_decoder_2_p1, bcd_to_7_segment_decoder_2_p2, bcd_to_7_segment_decoder_2_p3,
       bcd_to_7_segment_decoder_2_p4, bcd_to_7_segment_decoder_2_p6, bcd_to_7_segment_decoder_2_p7,
       bcd_to_7_segment_decoder_2_p8, bcd_to_7_segment_decoder_3_p1, bcd_to_7_segment_decoder_3_p2,
       bcd_to_7_segment_decoder_3_p3, bcd_to_7_segment_decoder_3_p4, bcd_to_7_segment_decoder_3_p6,
       bcd_to_7_segment_decoder_3_p7, bcd_to_7_segment_decoder_3_p8, bcd_to_7_segment_decoder_4_p1,
       bcd_to_7_segment_decoder_4_p2, bcd_to_7_segment_decoder_4_p3, bcd_to_7_segment_decoder_4_p4,
       bcd_to_7_segment_decoder_4_p6, bcd_to_7_segment_decoder_4_p7, bcd_to_7_segment_decoder_4_p8, BTND_out,
       BTNL_out, BTNR_out, BTNU_out, clock_1_out, clock_2_out, clock_3_out, comparator_1_eq, comparator_2_eq,
       comparator_3_eq, comparator_4_eq, counter_2_carry, d_ff_1_q, d_ff_2_q, d_ff_3_q, d_ff_4_q,
       multiplexer_1_out, multiplexer_2_out, multiplexer_3_out, multiplexer_4_out, multiplexer_6_out,
       multiplexer_8_out, multiplexer_9_out, multiplexer_11_out, not_1_out, not_2_out, or_1_out, or_2_out,
       or_3_out, undriven, undriven_2;
  wire [1:0] adjust_1_mux_out, counter_7_q;
  wire [2:0] adjust_1_time_hour_2, counter_3_q, counter_5_q, counter_6_q, multiplexer_7_out,
       multiplexer_10_out;
  wire [3:0] adjust_1_alarm_hour_1, adjust_1_alarm_hour_2, adjust_1_alarm_min_1, adjust_1_alarm_min_2,
       adjust_1_time_hour_1, adjust_1_time_min_1, adjust_1_time_min_2, bcd_to_7_segment_decoder_1_p5,
       bcd_to_7_segment_decoder_2_p5, counter_1_q, counter_2_q, counter_4_q, multiplexer_5_out,
       multiplexer_12_out, multiplexer_13_out, multiplexer_14_out, multiplexer_15_out, multiplexer_16_out,
       multiplexer_17_out, multiplexer_18_out, multiplexer_20_out, multiplexer_21_out, multiplexer_22_out,
       multiplexer_24_out, multiplexer_25_out;
  wire [6:0] adjust_1_out_6;

  Multiplexer multiplexer_1 (.in0(clock_1_out), .out(multiplexer_1_out), .sel(and_12_out));  // open: in1
  Clock clock_1 (.out(clock_1_out));
  Multiplexer multiplexer_2 (.in0(undriven), .in1(1'b1), .out(multiplexer_2_out), .sel(or_1_out));
  not not_1 (not_1_out, BTNC);
  Button BTNL (.out(BTNL_out));
  Button BTNR (.out(BTNR_out));
  Button BTND (.out(BTND_out));
  Button BTNU (.out(BTNU_out));
  Multiplexer multiplexer_3 (.in0(and_9_out), .in1(1'b1), .out(multiplexer_3_out), .sel(BTNC));
  Multiplexer multiplexer_4 (.in0(and_1_out), .in1(clock_2_out), .out(multiplexer_4_out), .sel(or_1_out));
  Clock clock_2 (.out(clock_2_out));
  and and_1 (and_1_out, multiplexer_1_out, not_1_out);
  Multiplexer #(.width(4)) multiplexer_5 (
    .in0(4'b0000), .in1(adjust_1_time_min_1), .out(multiplexer_5_out), .sel(BTNC));
  Multiplexer multiplexer_6 (.in0(and_8_out), .in1(1'b1), .out(multiplexer_6_out), .sel(BTNC));
  Multiplexer #(.width(3)) multiplexer_7 (
    .in0(3'b000), .in1(adjust_1_time_min_2[2:0]), .out(multiplexer_7_out), .sel(BTNC));
  or or_1 (or_1_out, BTNU_out, BTND_out, BTNR_out, BTNL_out);
  Multiplexer multiplexer_8 (.in0(and_5_out), .in1(1'b1), .out(multiplexer_8_out), .sel(or_1_out));
  or or_2 (or_2_out, and_2_out, and_6_out);
  Multiplexer multiplexer_9 (.in0(or_3_out), .in1(1'b1), .out(multiplexer_9_out), .sel(BTNC));
  Multiplexer #(.width(3)) multiplexer_10 (
    .in0(3'b000), .in1(adjust_1_time_hour_2), .out(multiplexer_10_out), .sel(BTNC));
  Counter #(.max('hf), .width(4)) counter_1 (
    .clr(in_1), .load(and_4_out), .count(1'b1), .clk(and_1_out), .D({in_5, in_4, in_3, in_2}), .Q(counter_1_q));  // open: up, carry
  Multiplexer multiplexer_11 (.in0(or_2_out), .in1(1'b1), .out(multiplexer_11_out), .sel(BTNC));
  Counter #(.max('hf), .width(4)) counter_2 (
    .clr(in_18), .load(multiplexer_11_out), .count(and_8_out), .clk(and_1_out), .D(multiplexer_12_out),
    .carry(counter_2_carry), .Q(counter_2_q));  // open: up
  Counter #(.max('h7), .width(3)) counter_3 (
    .clr(undriven_2), .load(and_5_out), .count(and_4_out), .clk(and_1_out), .D({in_9, in_8, in_7}),
    .Q(counter_3_q));  // open: up, carry
  Counter #(.max('hf), .width(4)) counter_4 (
    .clr(in_11), .load(multiplexer_3_out), .up(multiplexer_2_out), .count(multiplexer_8_out),
    .clk(multiplexer_4_out), .D(multiplexer_5_out), .Q(counter_4_q));  // open: carry
  Counter #(.max('h7), .width(3)) counter_5 (
    .clr(in_12), .load(multiplexer_6_out), .count(and_9_out), .clk(and_1_out), .D(multiplexer_7_out),
    .Q(counter_5_q));  // open: up, carry
  Counter #(.max('h7), .width(3)) counter_6 (
    .clr(in_19), .load(multiplexer_9_out), .count(and_6_out), .clk(and_1_out), .D(multiplexer_10_out),
    .Q(counter_6_q));  // open: up, carry
  or or_3 (or_3_out, and_2_out, and_7_out);
  Multiplexer #(.width(4)) multiplexer_12 (
    .in0(4'b0000), .in1(adjust_1_time_hour_1), .out(multiplexer_12_out), .sel(BTNC));
  and and_2 (and_2_out, counter_2_q[2], counter_6_q[1]);
  and and_3 (and_3_out, and_4_out, counter_3_q[0]);
  Adjust adjust_1 (
    .BTNL(BTNL_out), .BTNR(BTNR_out), .BTND(BTND_out), .BTNU(BTNU_out), .mux_out(adjust_1_mux_out),
    .out_6(adjust_1_out_6), .Time_min_1(adjust_1_time_min_1), .Time_min_2(adjust_1_time_min_2),
    .Time_Hour_1(adjust_1_time_hour_1), .Time_Hour_2({in_21, adjust_1_time_hour_2}),
    .Alarm_min_1(adjust_1_alarm_min_1), .Alarm_min_2(adjust_1_alarm_min_2),
    .Alarm_Hour_1(adjust_1_alarm_hour_1), .Alarm_Hour_2(adjust_1_alarm_hour_2));  // open: out_7, out_10, out_11, out_14, out_15, out_18, out_19
  and and_4 (and_4_out, counter_1_q[0], counter_1_q[3]);
  and and_5 (and_5_out, and_3_out, counter_3_q[2]);
  and and_6 (and_6_out, counter_2_q[0], and_8_out, counter_2_q[3]);
  and and_7 (and_7_out, counter_6_q[1], and_6_out);
  and and_8 (and_8_out, counter_5_q[2], and_9_out, counter_5_q[0]);
  and and_9 (and_9_out, counter_4_q[3], and_5_out, counter_4_q[0]);
  Multiplexer #(.width(4)) multiplexer_13 (
    .in0({in_20, counter_6_q}), .in1(multiplexer_21_out), .out(multiplexer_13_out), .sel(BTNC));
  // BCD_to_7_Segment_decoder bcd_to_7_segment_decoder_1: pin names not known; wires that end beside it: bcd_to_7_segment_decoder_1_p1, bcd_to_7_segment_decoder_1_p2, bcd_to_7_segment_decoder_1_p3, bcd_to_7_segment_decoder_1_p4, bcd_to_7_segment_decoder_1_p5, bcd_to_7_segment_decoder_1_p6, bcd_to_7_segment_decoder_1_p7, bcd_to_7_segment_decoder_1_p8
  Multiplexer #(.width(4)) multiplexer_14 (
    .in0(adjust_1_time_min_1), .in1(adjust_1_alarm_min_1), .out(multiplexer_14_out), .sel(adjust_1_mux_out[1]));
  Multiplexer #(.width(4)) multiplexer_15 (
    .in0(counter_4_q), .in1(multiplexer_14_out), .out(multiplexer_15_out), .sel(BTNC));
  Multiplexer #(.width(4)) multiplexer_16 (
    .in0(adjust_1_time_min_2), .in1(adjust_1_alarm_min_2), .out(multiplexer_16_out), .sel(adjust_1_mux_out[1]));
  _7_Segment_Display u_7_segment_display_1 (
    .g(bcd_to_7_segment_decoder_1_p1), .f(bcd_to_7_segment_decoder_1_p3), .a(bcd_to_7_segment_decoder_1_p6),
    .b(bcd_to_7_segment_decoder_1_p8), .e(bcd_to_7_segment_decoder_1_p2), .d(bcd_to_7_segment_decoder_1_p4),
    .c(bcd_to_7_segment_decoder_1_p7));  // open: dp
  Multiplexer #(.width(4)) multiplexer_17 (
    .in0({in_14, counter_5_q}), .in1(multiplexer_16_out), .out(multiplexer_17_out), .sel(BTNC));
  Multiplexer #(.width(4)) multiplexer_18 (
    .in0(adjust_1_time_hour_1), .in1(adjust_1_alarm_hour_1), .out(multiplexer_18_out),
    .sel(adjust_1_mux_out[1]));
  // BCD_to_7_Segment_decoder bcd_to_7_segment_decoder_2: pin names not known; wires that end beside it: bcd_to_7_segment_decoder_2_p1, bcd_to_7_segment_decoder_2_p2, bcd_to_7_segment_decoder_2_p3, bcd_to_7_segment_decoder_2_p4, bcd_to_7_segment_decoder_2_p5, bcd_to_7_segment_decoder_2_p6, bcd_to_7_segment_decoder_2_p7, bcd_to_7_segment_decoder_2_p8
  Multiplexer #(.select(2), .width(4)) multiplexer_19 (
    .in0(multiplexer_22_out), .out(bcd_to_7_segment_decoder_1_p5), .sel(counter_7_q));  // open: in1, in2, in3
  Multiplexer #(.width(4)) multiplexer_20 (
    .in0(counter_2_q), .in1(multiplexer_18_out), .out(multiplexer_20_out), .sel(BTNC));
  Multiplexer #(.width(4)) multiplexer_21 (
    .in0({in_21, adjust_1_time_hour_2}), .in1(adjust_1_alarm_hour_2), .out(multiplexer_21_out),
    .sel(adjust_1_mux_out[1]));
  Multiplexer #(.select(2), .width(4)) multiplexer_22 (
    .in0(multiplexer_13_out), .in1(multiplexer_20_out), .in2(multiplexer_17_out), .in3(multiplexer_15_out),
    .out(multiplexer_22_out), .sel(counter_7_q));
  Multiplexer #(.select(2), .width(4)) multiplexer_23 (
    .in1(multiplexer_22_out), .out(bcd_to_7_segment_decoder_2_p5), .sel(counter_7_q));  // open: in0, in2, in3
  Comparator #(.width(4)) comparator_1 (
    .a(adjust_1_alarm_hour_2), .b({in_20, counter_6_q}), .eq(comparator_1_eq));  // open: gt, lt
  Comparator #(.width(4)) comparator_2 (
    .a(adjust_1_alarm_hour_1), .b(counter_2_q), .eq(comparator_2_eq));  // open: gt, lt
  Comparator #(.width(4)) comparator_3 (
    .a({in_14, counter_5_q}), .b(adjust_1_alarm_min_2), .eq(comparator_3_eq));  // open: gt, lt
  Comparator #(.width(4)) comparator_4 (
    .a(counter_4_q), .b(adjust_1_alarm_min_1), .eq(comparator_4_eq));  // open: gt, lt
  _7_Segment_Display u_7_segment_display_2 (
    .g(bcd_to_7_segment_decoder_2_p1), .f(bcd_to_7_segment_decoder_2_p3), .a(bcd_to_7_segment_decoder_2_p6),
    .b(bcd_to_7_segment_decoder_2_p8), .e(bcd_to_7_segment_decoder_2_p2), .d(bcd_to_7_segment_decoder_2_p4),
    .c(bcd_to_7_segment_decoder_2_p7));  // open: dp
  Multiplexer #(.select(2), .width(4)) multiplexer_24 (
    .in2(multiplexer_22_out), .out(multiplexer_24_out), .sel(counter_7_q));  // open: in0, in1, in3
  // BCD_to_7_Segment_decoder bcd_to_7_segment_decoder_3: pin names not known; wires that end beside it: bcd_to_7_segment_decoder_3_p1, bcd_to_7_segment_decoder_3_p2, bcd_to_7_segment_decoder_3_p3, bcd_to_7_segment_decoder_3_p4, multiplexer_24_out, bcd_to_7_segment_decoder_3_p6, bcd_to_7_segment_decoder_3_p7, bcd_to_7_segment_decoder_3_p8
  Multiplexer #(.select(2), .width(4)) multiplexer_25 (
    .in3(multiplexer_22_out), .out(multiplexer_25_out), .sel(counter_7_q));  // open: in0, in1, in2
  and and_10 (and_10_out, comparator_3_eq, comparator_2_eq);
  and and_11 (and_11_out, comparator_1_eq, comparator_4_eq);
  _7_Segment_Display u_7_segment_display_3 (
    .g(bcd_to_7_segment_decoder_3_p1), .f(bcd_to_7_segment_decoder_3_p3), .a(bcd_to_7_segment_decoder_3_p6),
    .b(bcd_to_7_segment_decoder_3_p8), .e(bcd_to_7_segment_decoder_3_p2), .d(bcd_to_7_segment_decoder_3_p4),
    .c(bcd_to_7_segment_decoder_3_p7));  // open: dp
  Clock clock_3 (.out(clock_3_out));
  // BCD_to_7_Segment_decoder bcd_to_7_segment_decoder_4: pin names not known; wires that end beside it: bcd_to_7_segment_decoder_4_p1, bcd_to_7_segment_decoder_4_p2, bcd_to_7_segment_decoder_4_p3, bcd_to_7_segment_decoder_4_p4, multiplexer_25_out, bcd_to_7_segment_decoder_4_p6, bcd_to_7_segment_decoder_4_p7, bcd_to_7_segment_decoder_4_p8
  and and_12 (and_12_out, and_11_out, and_10_out);
  _7_Segment_Display u_7_segment_display_4 (
    .g(bcd_to_7_segment_decoder_4_p1), .f(bcd_to_7_segment_decoder_4_p3), .a(bcd_to_7_segment_decoder_4_p6),
    .b(bcd_to_7_segment_decoder_4_p8), .e(bcd_to_7_segment_decoder_4_p2), .d(bcd_to_7_segment_decoder_4_p4),
    .c(bcd_to_7_segment_decoder_4_p7));  // open: dp
  not not_2 (not_2_out, d_ff_4_q);
  D_Flip_Flop d_ff_1 (.D(not_2_out), .clk(clock_3_out), .Q(d_ff_1_q));  // open: Qn, preset, reset
  D_Flip_Flop d_ff_2 (.D(d_ff_1_q), .clk(clock_3_out), .Q(d_ff_2_q));  // open: Qn, preset, reset
  Counter #(.max('h3), .width(2)) counter_7 (
    .clr(in_13), .load(and_13_out), .up(1'b1), .clk(d_ff_4_q), .D({in_16, in_15}), .Q(counter_7_q));  // open: count, carry
  D_Flip_Flop d_ff_3 (.D(d_ff_2_q), .clk(clock_3_out), .Q(d_ff_3_q));  // open: Qn, preset, reset
  D_Flip_Flop d_ff_4 (.D(d_ff_3_q), .clk(clock_3_out), .Q(d_ff_4_q));  // open: Qn, preset, reset
  LED led_1 (.in(and_12_out));
  and and_13 (and_13_out, counter_7_q[0], counter_7_q[1]);
endmodule

module Adjust (
  input  BTNL,
  input  BTNR,
  input  BTND,
  input  BTNU,
  output [1:0] mux_out,
  output [6:0] out_6,
  output [6:0] out_7,
  output [3:0] Time_min_1,
  output [3:0] Time_min_2,
  output [6:0] out_10,
  output [6:0] out_11,
  output [3:0] Time_Hour_1,
  output [3:0] Time_Hour_2,
  output [6:0] out_14,
  output [6:0] out_15,
  output [3:0] Alarm_min_1,
  output [3:0] Alarm_min_2,
  output [6:0] out_18,
  output [6:0] out_19,
  output [3:0] Alarm_Hour_1,
  output [3:0] Alarm_Hour_2
);

  wire and_1_out, and_2_out, and_3_out, and_4_out, and_5_out, and_6_out, and_7_out, and_8_out, and_9_out,
       and_10_out, and_11_out, and_12_out, and_13_out, and_14_out, bcd_to_7_segment_decoder_3_p5,
       counter_6_carry, counter_8_carry, decoder_1_out0, decoder_1_out1, decoder_1_out2, decoder_1_out3,
       or_1_out, or_2_out, or_3_out, or_4_out;

  or or_1 (or_1_out, BTNL, BTNR);
  or or_2 (or_2_out, BTND, BTNU);
  Decoder #(.enable("false"), .select(2)) decoder_1 (
    .out0(decoder_1_out0), .out1(decoder_1_out1), .out2(decoder_1_out2), .out3(decoder_1_out3), .sel(mux_out));
  Counter #(.max('h3), .width(2)) counter_1 (
    .clr(1'b0), .up(BTNR), .clk(or_1_out), .D(2'b00), .Q(mux_out));  // open: load, count, carry
  and and_1 (and_1_out, decoder_1_out2, or_2_out);
  and and_2 (and_2_out, decoder_1_out1, BTNU);
  and and_3 (and_3_out, decoder_1_out1, or_2_out);
  and and_4 (and_4_out, decoder_1_out3, BTNU);
  and and_5 (and_5_out, decoder_1_out3, or_2_out);
  and and_6 (and_6_out, decoder_1_out2, BTNU);
  and and_7 (and_7_out, decoder_1_out0, BTNU);
  and and_8 (and_8_out, decoder_1_out0, or_2_out);
  Counter #(.max('h9), .width(4)) counter_2 (
    .clr(1'b0), .load(1'b0), .up(and_2_out), .count(1'b1), .clk(and_3_out), .Q(Time_min_1));  // open: D, carry
  Counter #(.max('h5), .width(3)) counter_3 (
    .clr(1'b0), .up(and_2_out), .count(and_10_out), .clk(and_3_out), .Q(Time_min_2[2:0]));  // open: load, D, carry
  Counter #(.max('h9), .width(4)) counter_4 (
    .clr(1'b0), .load(1'b0), .up(and_4_out), .count(1'b1), .clk(and_5_out), .Q(Alarm_min_1));  // open: D, carry
  Counter #(.max('h5), .width(3)) counter_5 (
    .clr(1'b0), .up(and_4_out), .count(and_11_out), .clk(and_5_out), .Q(Alarm_min_2[2:0]));  // open: load, D, carry
  Counter #(.max('h9), .width(4)) counter_6 (
    .clr(1'b0), .load(and_9_out), .up(and_6_out), .count(1'b1), .clk(and_1_out), .D(4'b0000),
    .carry(counter_6_carry), .Q(Alarm_Hour_1));
  Counter #(.max('h2), .width(3)) counter_7 (
    .clr(1'b0), .up(and_6_out), .count(or_3_out), .clk(and_1_out), .Q(Alarm_Hour_2[2:0]));  // open: load, D, carry
  or or_3 (or_3_out, and_9_out, and_12_out);
  Counter #(.max('h9), .width(4)) counter_8 (
    .clr(1'b0), .load(and_13_out), .up(and_7_out), .count(1'b1), .clk(and_8_out), .D(4'b0000),
    .carry(counter_8_carry), .Q(Time_Hour_1));
  Counter #(.max('h2), .width(3)) counter_9 (
    .clr(1'b0), .up(and_7_out), .count(or_4_out), .clk(and_8_out), .Q(Time_Hour_2[2:0]));  // open: load, D, carry
  and and_9 (and_9_out, Alarm_Hour_2[1], Alarm_Hour_1[0], Alarm_Hour_1[1]);
  and and_10 (and_10_out, Time_min_1[3], Time_min_1[0]);
  or or_4 (or_4_out, and_13_out, and_14_out);
  and and_11 (and_11_out, Alarm_min_1[3], Alarm_min_1[0]);
  and and_12 (and_12_out, Alarm_Hour_1[3], Alarm_Hour_1[0]);
  and and_13 (and_13_out, Time_Hour_2[1], Time_Hour_1[0], Time_Hour_1[1]);
  // BCD_to_7_Segment_decoder bcd_to_7_segment_decoder_1: pin names not known; wires that end beside it: out_18[0], out_18[4], out_18[1], out_18[5], out_18[2], out_18[6], out_18[3]
  and and_14 (and_14_out, Time_Hour_1[3], Time_Hour_1[0]);
  // BCD_to_7_Segment_decoder bcd_to_7_segment_decoder_2: pin names not known; wires that end beside it: out_14[0], out_14[4], out_14[1], out_14[5], out_14[2], out_14[6], out_14[3]
  // BCD_to_7_Segment_decoder bcd_to_7_segment_decoder_3: pin names not known; wires that end beside it: out_6[0], out_6[4], out_6[1], out_6[5], bcd_to_7_segment_decoder_3_p5, bcd_to_7_segment_decoder_3_p5, out_6[2], out_6[6], out_6[3]
  // BCD_to_7_Segment_decoder bcd_to_7_segment_decoder_4: pin names not known; wires that end beside it: counter_8_carry, out_10[0], out_10[4], out_10[1], out_10[5], out_10[2], out_10[6], out_10[3]
  // BCD_to_7_Segment_decoder bcd_to_7_segment_decoder_5: pin names not known; wires that end beside it: out_19[0], out_19[4], out_19[1], out_19[5], out_19[2], out_19[6], out_19[3]
  // BCD_to_7_Segment_decoder bcd_to_7_segment_decoder_6: pin names not known; wires that end beside it: out_7[0], out_7[4], out_7[1], out_7[5], out_7[2], out_7[6], out_7[3]
  // BCD_to_7_Segment_decoder bcd_to_7_segment_decoder_7: pin names not known; wires that end beside it: out_11[0], out_11[4], out_11[1], out_11[5], out_11[2], out_11[6], out_11[3]
  // BCD_to_7_Segment_decoder bcd_to_7_segment_decoder_8: pin names not known; wires that end beside it: out_15[0], out_15[4], out_15[1], out_15[5], out_15[2], out_15[6], out_15[3]

  assign Alarm_Hour_2[3] = 1'b0;
  assign Alarm_min_2[3] = 1'b0;
  assign Time_Hour_2[3] = 1'b0;
  assign Time_min_2[3] = 1'b0;
endmodule
